# Fritzing sketch IrProject (saved by Fritzing 1.0.5)
breadboards: 1

parts:
  A1 = ESP32 38Pin narrow
  OLED1 = OLED Mono 0.56 inch blue or white
  Mod1 = KY-022 Infrared Receiver Module [package="Breakout board"]
  VCC1 = 4 x AAA Battery Mount [internal_resistance=0.1Ω]
  Q1 = TRANSISTOR_NPN [package=to-92]
  R1 = Resistor [tolerance=±5% resistance=50 package="2010 [SMD]"]
  LED1 = smd LED [color="Red (633nm)" package="0805 [SMD]"]
  R2 = Resistor [tolerance=±5% resistance=220 package="1206 [SMD]"]

nets:
  VCC: A1.Pin_1, OLED1.VCC, Mod1.Vin
  N1: A1.Pin_14, A1.Pin_32, A1.Pin_38, OLED1.GND, Mod1.-, VCC1.-, Q1.E
  N2: A1.Pin_23, Mod1.S
  N3: A1.Pin_26, R2.Pin_1
  N4: A1.Pin_33, OLED1.SDA
  N5: A1.Pin_36, OLED1.SCL
  N6: VCC1.+, R1.Pin_1
  N7: Q1.B, R2.Pin_0
  N8: Q1.C, LED1.cathode
  N9: R1.Pin_0, LED1.anode

custom parts:
  ESP32 38Pin narrow: ESP32 38Pin narrow.
  OLED Mono 0.56 inch blue or white: OLED, I2C 3.3V - 5V Blue and White text versions
  KY-022 Infrared Receiver Module: KY-022 IR receiver module, reacts to 38kHz infrared light.
